# Fritzing sketch foosbot (saved by Fritzing 0.9.2b)

parts:
  Raspberry_Pi1 = Raspberry Pi 2
  S2 = Pushbutton [package=THT]
  J2 = Infrared Proximity Sensor
  J3 = Infrared Proximity Sensor

nets:
  N1: Raspberry_Pi1.GPIO26, J3.Vout
  N2: Raspberry_Pi1.GPIO21, S2.leg1
  N3: Raspberry_Pi1.GPIO20, J2.Vout
  GND: Raspberry_Pi1.GND, J3.GND
  5V: Raspberry_Pi1.5V, J3.Vcc

notes:
  5v power
  GPIO 20 to Red ball return
  GPIO 26 to Black ball return
  GPIO 21 to reset button
  Ground
  Only one side of the IR sensor send a signal to the GPIO. The other side just needs 5v power and ground. Not shown here.
